# Fritzing sketch IntruderAlert (saved by Fritzing 0.9.3b)

parts:
  R1 = BBC MicroBit
  R2 = Photocell (LDR) [package=THT]
  SP1 = SPEAKER [package=pcb_mount_speaker]
  LD1 = LD
  BATT1 = 3xAAA Switchable Battery Pack w/Bare Wire

nets:
  N1: R1.GND, SP1.+
  N2: R1.3v3, R2.pin_0
  N3: R1.P1_ANALOG_IN, R2.pin_1
  N4: R1.P0_ANALOG_IN, SP1.-
  N5: LD1.cathode, BATT1.NEG
  N6: LD1.anode, BATT1.POS

notes:
  The red wire, connects Pin 0 to the tip of your speaker jack.
  The black wire connects GND to the lowest ring of the jack.

custom parts:
  BBC MicroBit: The BBC MICRO:BIT
  LD: A Generic Red Dot Laser Diode Module (~5mW)
  3xAAA Switchable Battery Pack w/Bare Wire: 3xAAA Switchable Battery Pack w/Bare Wire Connectors
